# Fritzing sketch TSFRL_master_module (saved by Fritzing 0.9.0b)

parts:
  IC1 = Voltage Regulator [package=to220-igo]
  C1 = Capacitor Polarized [package=cpol-radial-100uf-25v]
  R1 = Resistor [tolerance=±5% resistance=220 package=THT]
  POWER = LED - 3mm [color="Red (633nm)" package="3 mm [THT]"]
  KEYS_pins = rounded female pin header, 8 pins [form="♀ (female rounded)"]
  IC2 = Hex Inverter Schmitt Trigger SN74HC14 [package="DIP (Dual Inline)"]
  DATA_pins = male pin header, 5 pins [form="♂ (male)"]
  TEST = LED - 3mm [color="Blue (525nm)" current=20pA package="3 mm [THT]"]
  DATA = LED - 3mm [color="Yellow (595nm)" package="3 mm [THT]"]
  ERROR = LED - 3mm [color="Red (633nm)" package="3 mm [THT]"]
  DONE = LED - 3mm [color="Green (570nm)" package="3 mm [THT]"]
  Part1 = Arduino Nano (Rev3.0)
  LCD_pins = male pin header, 2 pins [form="♂ (male)"]
  R2 = Resistor [tolerance=±5% resistance=220 package=THT]
  R3 = Resistor [tolerance=±5% resistance=220 package=THT]
  R4 = Resistor [tolerance=±5% resistance=220 package=THT]
  R5 = Resistor [tolerance=±5% resistance=220 package=THT]
  U2 = DS75176BN [package=dil08]
  C2 = Capacitor Polarized [package=cpol-radial-10uf-16v]

nets:
  GND: IC1.GND, C1.-, POWER.cathode, KEYS_pins.pin1, IC2.GND, DATA_pins.pin2, TEST.cathode, DATA.cathode, ERROR.cathode, DONE.cathode, Part1.GND, U2.GND, C2.-
  12V: IC1.IN, C1.+
  N1: IC1.OUT, R1.Pin_0, C2.+
  5V: R1.Pin_1, POWER.anode, KEYS_pins.pin8, IC2.VCC, DATA_pins.pin1, Part1.5V, U2.VCC
  N2: KEYS_pins.pin2, DATA_pins.pin5, Part1.RESET
  N3: KEYS_pins.pin3, IC2.3A
  N4: KEYS_pins.pin4, IC2.2A
  N5: KEYS_pins.pin5, IC2.1A
  N6: KEYS_pins.pin6, IC2.4A
  N7: KEYS_pins.pin7, IC2.5A
  N8: IC2.1Y, Part1.D5
  N9: IC2.2Y, Part1.D4
  N10: IC2.3Y, Part1.D3
  N11: IC2.4Y, Part1.D6
  N12: IC2.5Y, Part1.D7
  N13: DATA_pins.pin3, U2.DO/RI#5
  N14: DATA_pins.pin4, U2.DO/RI#6
  N15: TEST.anode, R5.Pin_1
  N16: DATA.anode, R2.Pin_1
  N17: ERROR.anode, R3.Pin_1
  N18: DONE.anode, R4.Pin_1
  N19: Part1.D8, R5.Pin_0
  N20: Part1.D9, R4.Pin_0
  N21: Part1.D10, R3.Pin_0
  N22: Part1.D11/MOSI, U2.DI
  N23: Part1.D12/MISO, U2.RO
  N24: Part1.A5, LCD_pins.pin1
  N25: Part1.A4, LCD_pins.pin2
  N26: Part1.D13/SCK, R2.Pin_0, U2.RE, U2.DE

notes:
  TSFRL_master_module_keys
  8) +5v
  7) keyUP
  6) keyRIGHT
  5) keyLEFT
  4) keyDOWN
  3)keySTART
  2)keySTOP/CANCEL
  1)GND
  SDA(LCD)
  SCL(LCD)
  GND
  keySTOP/CANCEL
  keySTART
  keyDOWN
  keyLEFT
  keyRIGHT
  keyUP
  VCC +5V
  CANCEL signal
  RS485_a
  RS485_b
  Test Stand For Radio Lamps, Test Stand For Radio Lamps project: master module, 1.0

custom parts:
  DS75176BN: RS-485 transceiver
  Capacitor Polarized: Capacitor Polarized cpol-radial-10uf-16v
